# Fritzing sketch arducar_schematic (saved by Fritzing 0.8.7b)

parts:
  Parte1 = Arduino Uno (Rev3)
  VCC1 = 4 x AAA Battery Mount
  Magnetometer = Triple Axis Magnetometer - HMC5883 Breakout
  Parte4 = Arduino Motor Shield (Rev3)
  VCC2 = 4 x AAA Battery Mount
  M2 = DC Motor
  M1 = DC Motor
  R1 = Resistor [tolerance=±5% resistance=10k package=THT]
  R2 = Resistor [tolerance=±5% resistance=10k package=THT]

nets:
  N1: Parte1.A4/SDA, Magnetometer.SCL, R2.Pin_1
  N2: Parte1.A5/SCL, Magnetometer.SDA, R1.Pin_1
  3V3: Parte1.3V3, Magnetometer.VCC, R1.Pin_0, R2.Pin_0
  GND: Parte1.GND, VCC1.-, Magnetometer.GND
  N3: Parte1.VIN, VCC1.+
  N4: Parte4.GND, VCC2.-
  N5: Parte4.B-, M1.pin_2
  N6: Parte4.B+, M1.pin_1
  N7: Parte4.A-, M2.pin_2
  N8: Parte4.A+, M2.pin_1
  N9: Parte4.VMOT, VCC2.+

notes:
  Green --> SCL
  Orange --> SDA
  Motorshield should be configured to draw power from external batteries
  Motor shield on top of Arduino UNO Rev.3
